# Fritzing sketch testbench (saved by Fritzing 0.9.3b)
breadboards: 1

parts:
  M1 = STM32F103C8T6 blue mini board
  U1 = LCD-16X2 [package=lcd-16x2_noholes]
  U2 = POT [package=pot_mammoth]
  S1 = Pushbutton [package="[SMD]"]
  S2 = Pushbutton [package="[SMD]"]
  S3 = Pushbutton [package="[SMD]"]
  Bauteil1 = FTDI Basic Programmer
  R1 = Resistor [tolerance=±5% resistance=4.7k package="0603 [SMD]"]
  R2 = Resistor [tolerance=±5% resistance=4.7k package="0603 [SMD]"]
  R3 = Resistor [tolerance=±5% resistance=4.7k package="0603 [SMD]"]
  LED1 = LED - 3mm [color="Red (633nm)" package="3 mm [THT]"]
  LED2 = LED - 3mm [color="Blue (470nm)" package="3 mm [THT]"]
  R4 = Resistor [tolerance=±5% resistance=220 package="0603 [SMD]"]
  R5 = Resistor [tolerance=±5% resistance=220 package="0603 [SMD]"]

nets:
  N1: M1.A12, LED1.cathode
  N2: M1.A15, LED2.cathode
  N3: M1.B4, U1.E
  N4: M1.B5, U1.RS
  N5: M1.B6, U1.DB4
  N6: M1.B7, U1.DB5
  N7: M1.B8, U1.DB6
  N8: M1.B9, U1.DB7
  GND: M1.G, M1.GND, U1.VSS, U1.R_W, U1.K, U2.S, Bauteil1.GND, R1.Pin_1, R2.Pin_1, R3.Pin_1, R4.Pin_0, R5.Pin_0
  N9: M1.3.3V, U2.E, Bauteil1.POWER
  N10: M1.A5, S3.Pin_3, S3.Pin_4, R3.Pin_0
  N11: M1.A6, S2.Pin_3, S2.Pin_4, R2.Pin_0
  N12: M1.A7, S1.Pin_3, S1.Pin_4, R1.Pin_0
  N13: U1.VDD, U1.A, S1.Pin_1, S1.Pin_2, S2.Pin_1, S2.Pin_2, S3.Pin_1, S3.Pin_2
  N14: U1.VO, U2.A
  N15: LED1.anode, R5.Pin_1
  N16: LED2.anode, R4.Pin_1
