# Fritzing sketch testbench (saved by Fritzing 0.9.3b)
circuit board: 8.46667cm x 5.64444cm
breadboards: 1

parts:
  U1 = LCD-16X2 [package=lcd-16x2_noholes]
  S1 = Pushbutton [package="[SMD]"]
  S2 = Pushbutton [package="[SMD]"]
  WeMos_D1_Mini2 = WeMos D1 Mini
  R2 = Resistor [tolerance=±5% resistance=4.7k package=THT]
  R1 = Resistor [tolerance=±5% resistance=4.7k package=THT]

nets:
  N1: U1.VSS, U1.VO, U1.R_W, U1.K, WeMos_D1_Mini2.G, R2.Pin_1, R1.Pin_1
  VDD: U1.VDD, U1.A, S1.Pin_1, S1.Pin_2, S2.Pin_1, S2.Pin_2, WeMos_D1_Mini2.3V3
  N2: U1.RS, WeMos_D1_Mini2.D3
  N3: U1.E, WeMos_D1_Mini2.D2
  N4: U1.DB4, WeMos_D1_Mini2.D5
  N5: U1.DB5, WeMos_D1_Mini2.D6
  N6: U1.DB6, WeMos_D1_Mini2.D7
  N7: U1.DB7, WeMos_D1_Mini2.D8
  N8: S1.Pin_3, S1.Pin_4, WeMos_D1_Mini2.D1, R1.Pin_0
  N9: S2.Pin_3, S2.Pin_4, WeMos_D1_Mini2.D0, R2.Pin_0
